# Fritzing sketch keypad && led (saved by Fritzing 1.0.5)
breadboards: 1

parts:
  Part1 = Arduino Uno (Rev3)
  LED1 = LED - 5mm [color="Red (633nm)" current=0.030A package="5 mm [THT]"]
  Matrix_keypad1 = KEYPAD 4x4
  R1 = Resistor [tolerance=±5% power=0.25W resistance=220 package=THT]

nets:
  N1: Part1.D8, Matrix_keypad1.row3
  N2: Part1.D9_PWM, Matrix_keypad1.row4
  N3: Part1.D12/MISO, R1.Pin_1
  N4: Part1.GND, LED1.cathode
  N5: Part1.D2, Matrix_keypad1.col1
  N6: Part1.D3_PWM, Matrix_keypad1.col2
  N7: Part1.D4, Matrix_keypad1.col3
  N8: Part1.D5_PWM, Matrix_keypad1.col4
  N9: Part1.D6_PWM, Matrix_keypad1.row1
  N10: Part1.D7, Matrix_keypad1.row2
  N11: LED1.anode, R1.Pin_0

custom parts:
  KEYPAD 4x4: Matrix keypad 16 buttons, 4 rows x 4 columns
